// Logisim project alu.circ as structural Verilog: 2 circuits, main circuit alu
module alu (
  input  [31:0] A,
  input  [31:0] B,
  input  [3:0] ALUSel,
  output [31:0] Result,
  output [31:0] out_5,
  output [31:0] out_6
);

  wire comparator_1_lt;
  wire [31:0] add0, and0, divu0, h32b_1_out_2, h32b_2_out_2, mulh0, multiplier_2_out, multiplier_3_out, or0,
       remu0, sll0, slt0, sra0, srl0, sub0, undefined0, xor0;

  Multiplexer #(.select(4), .width(32), .enable("false")) multiplexer_1 (
    .in0(add0), .in1(and0), .in2(or0), .in3(xor0), .in4(srl0), .in5(sra0), .in6(sll0), .in7(slt0),
    .in8(divu0), .in9(remu0), .in10(out_5), .in11(out_6), .in12(sub0), .in13(B), .in14(mulh0),
    .in15(undefined0), .out(Result), .sel(ALUSel));
  Adder #(.width(32)) adder_1 (.a(A), .b(B), .out(add0));  // open: cin, cout
  assign and0 = A & B;  // AND_Gate and_1, 32 bits wide
  assign or0 = A | B;  // OR_Gate or_1, 32 bits wide
  assign xor0 = A ^ B;  // XOR_Gate xor_1, 32 bits wide
  Shifter #(.width(32), .shift("lr")) shifter_1 (.in(A), .\dist (B[4:0]), .out(srl0));
  Shifter #(.width(32), .shift("ar")) shifter_2 (.in(A), .\dist (B[4:0]), .out(sra0));
  Shifter #(.width(32)) shifter_3 (.in(A), .\dist (B[4:0]), .out(sll0));
  Comparator #(.width(32)) comparator_1 (.a(A), .b(B), .lt(comparator_1_lt));  // open: gt, eq
  assign slt0 = {{31{1'b0}}, comparator_1_lt};  // Bit_Extender bit_extender_1
  Divider #(.width(32)) divider_1 (.a(A), .b(B), .out(divu0), .rem(remu0));  // open: upper
  Multiplier #(.width(32)) multiplier_1 (.a(A), .b(B), .out(out_5), .cout(out_6));  // open: cin
  Subtractor #(.width(32)) subtractor_1 (.a(A), .b(B), .out(sub0));  // open: bin, bout
  h32b h32b_1 (.in_1(A), .out_2(h32b_1_out_2));
  h32b h32b_2 (.in_1(B), .out_2(h32b_2_out_2));
  Multiplier #(.width(32)) multiplier_2 (.a(A), .b(h32b_2_out_2), .out(multiplier_2_out));  // open: cin, cout
  Multiplier #(.width(32)) multiplier_3 (.a(h32b_1_out_2), .b(B), .out(multiplier_3_out), .cin(out_6));  // open: cout
  Adder #(.width(32)) adder_2 (.a(multiplier_2_out), .b(multiplier_3_out), .out(mulh0));  // open: cin, cout

  // Other names for the same wires on the sheet: bsel0[31:0] = B; mul0[31:0] = out_5; mulhu0[31:0] = out_6

  // Notes on the sheet:
  //   INPUTS to your circuit
  //   DON'T CHANGE THE LOCATIONS OF THE INPUTS AND OUTPUTS!
  //   OUTPUT from your circuit
endmodule

module h32b (
  input  [31:0] in_1,
  output [31:0] out_2
);

  wire comparator_1_gt, not_1_out;

  Comparator #(.width(32)) comparator_1 (.a({32{1'b0}}), .b(in_1), .gt(comparator_1_gt));  // open: eq, lt
  Multiplexer #(.width(32), .enable("false")) multiplexer_1 (
    .in0({32{1'b1}}), .in1({32{1'b0}}), .out(out_2), .sel(not_1_out));
  not not_1 (not_1_out, comparator_1_gt);

  // Notes on the sheet:
  //   input
  //   output
endmodule
