// Logisim project control_logic.circ as structural Verilog: 1 circuit, main circuit control_logic
module control_logic (
  input  [31:0] inst,
  input  BrEq,
  input  BrLt,
  output PCSel,
  output RegWEn,
  output [2:0] ImmSel,
  output BrUn,
  output ASel,
  output BSel,
  output [3:0] ALUSel,
  output MemRW,
  output [1:0] WBSel
);

  wire and_1_out, and_2_out, and_5_out, and_6_out, and_7_out, and_8_out, and_9_out, and_11_out, and_12_out,
       and_13_out, and_14_out, and_15_out, and_16_out, and_17_out, and_18_out, and_21_out, and_26_out,
       and_28_out, and_29_out, and_30_out, and_31_out, and_32_out, and_34_out, not_1_out, not_2_out,
       not_3_out, not_4_out, not_5_out, not_6_out, not_7_out, not_8_out, not_9_out, not_10_out, not_11_out,
       not_12_out, not_13_out, not_14_out, not_15_out, not_16_out, not_17_out, not_18_out, not_19_out,
       not_20_out, not_21_out, not_22_out, not_23_out, not_24_out, not_25_out, not_26_out, not_27_out,
       not_28_out, not_29_out, not_30_out, not_31_out, not_32_out, not_33_out, or_1_out, or_2_out, or_3_out,
       or_4_out, or_5_out, xnor_1_out, xnor_2_out, xnor_3_out, xnor_4_out;
  wire [3:0] multiplexer_2_out;
  wire [4:0] multiplexer_1_out;
  wire [4:3] and_3_out;

  not not_1 (not_1_out, inst[5]);
  not not_2 (not_2_out, inst[13]);
  not not_3 (not_3_out, and_1_out);
  and and_1 (and_1_out, inst[12], not_2_out);
  not not_4 (not_4_out, inst[2]);
  not not_5 (not_5_out, inst[3]);
  not not_6 (not_6_out, inst[6]);
  not not_7 (not_7_out, inst[4]);
  and and_2 (and_2_out, not_1_out, not_3_out);
  and and_3 (and_3_out[3], inst[25], not_8_out);
  and and_4 (and_3_out[4], inst[30], not_8_out);
  not not_8 (not_8_out, and_2_out);
  and and_5 (and_5_out, not_4_out, not_5_out, not_6_out);
  xnor xnor_1 (xnor_1_out, inst[5], inst[4]);
  xnor xnor_2 (xnor_2_out, inst[2], inst[5]);
  and and_6 (and_6_out, not_5_out, inst[4], not_6_out);
  and and_7 (and_7_out, inst[6], not_7_out, inst[5], inst[2]);
  Multiplexer #(.width(5), .enable("false")) multiplexer_1 (
    .in0({and_3_out, inst[14:12]}), .in1({5{1'b0}}), .out(multiplexer_1_out), .sel(inst[6]));
  and and_8 (and_8_out, and_5_out, xnor_1_out);
  or or_1 (or_1_out, and_8_out, and_9_out, and_7_out);
  and and_9 (and_9_out, xnor_2_out, and_6_out);
  Multiplexer #(.select(5), .width(4), .enable("false")) multiplexer_2 (
    .in0(4'b0000), .in1(4'b0110), .in3(4'b0111), .in4(4'b0011), .in5(4'b0100), .in6(4'b0010), .in7(4'b0001),
    .in8(4'b1010), .in9(4'b1110), .in11(4'b1011), .in13(4'b1000), .in15(4'b1001), .in16(4'b1100),
    .in21(4'b0101), .out(multiplexer_2_out), .sel(multiplexer_1_out));  // open: in2, in10, in12, in14, in17, in18, in19, in20, in22, in23, in24, in25, in26, in27, in28, in29, in30, in31
  not not_9 (not_9_out, inst[6]);
  and and_10 (RegWEn, inst[0], inst[1], or_1_out);
  Multiplexer #(.width(4), .enable("false")) multiplexer_3 (
    .in0(multiplexer_2_out), .in1(4'b1101), .out(ALUSel), .sel(and_11_out));
  and and_11 (and_11_out, not_9_out, inst[2]);
  not not_10 (not_10_out, inst[6]);
  not not_11 (not_11_out, inst[4]);
  not not_12 (not_12_out, inst[2]);
  not not_13 (not_13_out, inst[4]);
  not not_14 (not_14_out, inst[2]);
  not not_15 (not_15_out, inst[3]);
  not not_16 (not_16_out, inst[4]);
  not not_17 (not_17_out, inst[5]);
  not not_18 (not_18_out, inst[6]);
  and and_12 (and_12_out, inst[6], not_11_out, not_12_out);
  and and_13 (and_13_out, not_10_out, inst[4], inst[2]);
  and and_14 (and_14_out, inst[5], inst[1], inst[0]);
  not not_19 (not_19_out, inst[6]);
  xnor xnor_3 (xnor_3_out, inst[2], inst[4]);
  xnor xnor_4 (xnor_4_out, inst[2], inst[3]);
  and and_15 (and_15_out, not_14_out, not_15_out, not_17_out, not_18_out);
  and and_16 (and_16_out, not_14_out, not_15_out, not_16_out, inst[5]);
  and and_17 (and_17_out, inst[2], not_15_out, inst[4], inst[5], not_18_out);
  and and_18 (and_18_out, inst[2], not_16_out, inst[5], inst[6]);
  and and_19 (ImmSel[1], or_3_out, and_14_out);
  and and_20 (ImmSel[0], inst[0], inst[1], inst[5], not_19_out, xnor_3_out);
  and and_21 (and_21_out, inst[0], inst[1], not_13_out, inst[5], inst[6]);
  or or_2 (or_2_out, and_15_out, and_16_out, and_17_out, and_18_out);
  or or_3 (or_3_out, and_12_out, and_13_out);
  and and_22 (ASel, and_21_out, xnor_4_out);
  and and_23 (BSel, inst[0], inst[1], or_2_out);
  not not_20 (not_20_out, inst[12]);
  not not_21 (not_21_out, inst[13]);
  not not_22 (not_22_out, inst[14]);
  not not_23 (not_23_out, BrLt);
  not not_24 (not_24_out, BrEq);
  not not_25 (not_25_out, inst[2]);
  not not_26 (not_26_out, inst[3]);
  not not_27 (not_27_out, inst[4]);
  not not_28 (not_28_out, inst[6]);
  and and_24 (BrUn, inst[13], inst[14]);
  and and_25 (WBSel[1], inst[0], inst[1], inst[2], not_29_out, inst[5], inst[6]);
  not not_29 (not_29_out, inst[4]);
  not not_30 (not_30_out, inst[2]);
  not not_31 (not_31_out, inst[3]);
  not not_32 (not_32_out, inst[6]);
  and and_26 (and_26_out, inst[2], inst[4]);
  not not_33 (not_33_out, inst[2]);
  and and_27 (MemRW, inst[0], inst[1], not_25_out, not_26_out, not_27_out, inst[5], not_28_out);
  or or_4 (or_4_out, not_30_out, and_26_out);
  and and_28 (and_28_out, inst[2], inst[6]);
  and and_29 (and_29_out, inst[6], not_33_out);
  and and_30 (and_30_out, not_20_out, not_21_out, not_22_out, not_23_out, BrEq);
  and and_31 (and_31_out, inst[12], not_21_out, not_22_out, not_24_out);
  and and_32 (and_32_out, not_20_out, inst[14], BrLt, not_24_out);
  and and_33 (WBSel[0], inst[0], inst[1], not_31_out, inst[4], not_32_out, or_4_out);
  or or_5 (or_5_out, and_30_out, and_31_out, and_32_out);
  or or_6 (PCSel, and_28_out, and_34_out);
  and and_34 (and_34_out, and_29_out, or_5_out);

  assign ImmSel[2] = inst[3];

  // Other names for the same wires on the sheet: func3[2:0] = inst[14:12]; opcode[6:0] = inst[6:0];
  //   func7[6:0] = inst[31:25]

  // Notes on the sheet:
  //   INPUTS to your circuit
  //   DON'T CHANGE THE LOCATIONS OF THE INPUTS AND OUTPUTS!
  //   OUTPUT from your circuit
endmodule
