// Logisim project cpu.circ as structural Verilog: 1 circuit, main circuit main
module main (
  input  [31:0] INSTRUCTION,
  input  CLOCK,
  output [31:0] PROGRAM_COUNTER,
  output [31:0] ra,
  output [31:0] sp,
  output [31:0] t0,
  output [31:0] t1,
  output [31:0] t2,
  output [31:0] s0,
  output [31:0] s1,
  output [31:0] a0,
  output [31:0] out_12,
  output [4:0] out_13,
  output out_14,
  output [1:0] out_15,
  output [31:0] out_16,
  output [3:0] out_17,
  output [2:0] out_18
);

  wire branch_comp_1_breq, branch_comp_1_brlt, control_logic_1_asel, control_logic_1_brun,
       control_logic_1_bsel, control_logic_1_memrw, control_logic_1_pcsel, not_1_out, not_2_out, or_1_out;
  wire [4:0] rs1, rs2;
  wire [31:0] adder_1_out, DMEM_p5, multiplexer_1_out, multiplexer_2_out, multiplexer_3_out,
       multiplexer_4_out, multiplexer_5_out, PC0, RegFile_read_data_1, RegFile_read_data_2, register_1_q,
       register_2_q;

  Multiplexer #(.width(32), .enable("false")) multiplexer_1 (
    .in0(INSTRUCTION), .in1({32{1'b0}}), .out(multiplexer_1_out), .sel(control_logic_1_pcsel));
  // AND_Gate and_1 has open pins: in0=or_1_out, in1=control_logic_1_bsel, in2=not_1_out, in3=not_2_out, out=open
  or or_1 (or_1_out, branch_comp_1_brlt, branch_comp_1_breq);
  not not_1 (not_1_out, out_15[1]);
  Register #(.width(32)) register_1 (
    .D(multiplexer_1_out), .clk(CLOCK),
    .Q({register_1_q[31:25], rs2, rs1, register_1_q[14:12], out_13, register_1_q[6:0]}));  // open: en, clr
  not not_2 (not_2_out, out_15[0]);
  control_logic control_logic_1 (
    .BSel(control_logic_1_bsel), .BrUn(control_logic_1_brun), .RegWEn(out_14), .ImmSel(out_18),
    .ASel(control_logic_1_asel), .PCSel(control_logic_1_pcsel), .BrLt(branch_comp_1_brlt),
    .BrEq(branch_comp_1_breq),
    .inst({register_1_q[31:25], rs2, rs1, register_1_q[14:12], out_13, register_1_q[6:0]}), .ALUSel(out_17),
    .MemRW(control_logic_1_memrw), .WBSel(out_15));
  Adder #(.width(32)) adder_1 (.a(PROGRAM_COUNTER), .b(32'h4), .out(adder_1_out));  // open: cin, cout
  Register #(.width(32)) PC (.D(multiplexer_2_out), .clk(CLOCK), .Q(PROGRAM_COUNTER));  // open: en, clr
  Multiplexer #(.width(32), .enable("false")) multiplexer_2 (
    .in0(adder_1_out), .in1(out_12), .out(multiplexer_2_out), .sel(control_logic_1_pcsel));
  imm_gen imm_gen_1 (
    .ImmSel(out_18), .inst({register_1_q[31:25], rs2, rs1, register_1_q[14:12], out_13, register_1_q[6:0]}),
    .imm(out_16));
  Register #(.width(32)) register_2 (.D(adder_1_out), .clk(CLOCK), .Q(register_2_q));  // open: en, clr
  Register #(.width(32)) register_3 (.D(PROGRAM_COUNTER), .clk(CLOCK), .Q(PC0));  // open: en, clr
  regfile_main RegFile (
    .rs2(rs2), .rd(out_13), .Read_Data_1(RegFile_read_data_1), .Read_Data_2(RegFile_read_data_2), .ra(ra),
    .sp(sp), .t0(t0), .t1(t1), .t2(t2), .s0(s0), .s1(s1), .a0(a0), .rs1(rs1), .Write_Data(multiplexer_5_out),
    .RegWEn(out_14), .clk(CLOCK));
  branch_comp branch_comp_1 (
    .BrEq(branch_comp_1_breq), .BrUn(control_logic_1_brun), .rs1(RegFile_read_data_1),
    .BrLt(branch_comp_1_brlt), .rs2(RegFile_read_data_2));
  Multiplexer #(.width(32), .enable("false")) multiplexer_3 (
    .in0(RegFile_read_data_1), .in1(PC0), .out(multiplexer_3_out), .sel(control_logic_1_asel));
  Multiplexer #(.width(32), .enable("false")) multiplexer_4 (
    .in0(RegFile_read_data_2), .in1(out_16), .out(multiplexer_4_out), .sel(control_logic_1_bsel));
  alu Arithmetic_Logic_Unit (
    .ALUSel(out_17), .Result(out_12), .A(multiplexer_3_out), .B(multiplexer_4_out));  // open: out_4
  // mem_main DMEM: pin names not known; wires that end beside it: out_12, RegFile_read_data_2, CLOCK, control_logic_1_memrw, DMEM_p5
  Multiplexer #(.select(2), .width(32), .enable("false")) multiplexer_5 (
    .in0(DMEM_p5), .in1(out_12), .in2(register_2_q), .out(multiplexer_5_out), .sel(out_15));  // open: in3

  // Other names for the same wires on the sheet: rd[4:0] = out_13; clk = CLOCK

  // Notes on the sheet:
  //   Output
  //   IMEM (do **NOT** move this)
  //   Inputs
  //   It is OK to move the PC, RegFile, ALU, MEM, Branch Comp, Imm Gen, and Control Logic to wherever is most convenient for you when constructing your CPU, and to delete this text
  //   Inputs/Outputs for testing. Do **NOT** move these.
endmodule
