// Logisim project imm_gen.circ as structural Verilog: 1 circuit, main circuit imm_gen
module imm_gen (
  input  [31:0] inst,
  input  [2:0] ImmSel,
  output [31:0] imm
);

  wire [0:0] undriven;
  wire [11:0] immU;
  wire [31:0] immI, immS, immSB, immUJ;

  Bit_Extender #(.in_width(32), .out_width(20)) bit_extender_1 (.in(immUJ), .out({inst[19:12], inst[31:20]}));
  assign immS = {{20{inst[31]}}, {inst[31:25], inst[11:7]}};  // Bit_Extender bit_extender_2
  assign immI = {{20{inst[31]}}, inst[31:20]};  // Bit_Extender bit_extender_3
  assign immSB = {{19{inst[31]}}, {inst[31], inst[7], inst[30:25], inst[11:8], undriven[0]}};  // Bit_Extender bit_extender_4
  Multiplexer #(.select(3), .width(32), .enable("false")) multiplexer_1 (
    .in0(immI), .in1(immS), .in2(immSB), .in3({inst[31:12], immU}), .in4(immUJ), .out(imm), .sel(ImmSel));  // open: in5, in6, in7

  // Other names for the same wires on the sheet: immU[31:12] = inst[31:12]

  // Notes on the sheet:
  //   INPUTS to your circuit
  //   DON'T CHANGE THE LOCATIONS OF THE INPUTS AND OUTPUTS!
  //   OUTPUT from your circuit
endmodule
